# Fritzing sketch schematic (saved by Fritzing 0.8.7b)
breadboards: 1

parts:
  Mod1 = Raspberry Pi Pico
  S2 = Pushbutton [package="[THT]"]
  S3 = Pushbutton [package="[THT]"]
  S4 = Pushbutton [package="[THT]"]
  Εξάρτημα1 = LCD1602-I2C
  A1 = HuskyLens-Vision-Sensor_1
  J2 = Basic Servo
  R1 = Resistor [tolerance=±5% resistance=220 package=THT]
  R2 = Resistor [tolerance=±5% resistance=220 package=THT]

nets:
  N1: Mod1.pin_1, A1.pin2
  N2: Mod1.pin_2, A1.pin1
  GND: Mod1.pin_3, Mod1.pin_8, Mod1.pin_13, Mod1.pin_18, Mod1.pin_23, Mod1.pin_28, Mod1.pin_33, Mod1.pin_38, Mod1.pin_42, Εξάρτημα1.GND, A1.pin3, J2.gnd
  N3: Mod1.pin_6, Εξάρτημα1.SDA, R2.Pin_1
  N4: Mod1.pin_7, Εξάρτημα1.SCL, R1.Pin_1
  N5: Mod1.pin_14, J2.pulse
  N6: Mod1.pin_15, S2.Pin_3, S2.Pin_4
  N7: Mod1.pin_19, S3.Pin_3, S3.Pin_4
  N8: Mod1.pin_20, S4.Pin_3, S4.Pin_4
  N9: Mod1.pin_36, S2.Pin_1, S2.Pin_2, S3.Pin_1, S3.Pin_2, S4.Pin_1, S4.Pin_2
  VCC: Mod1.pin_40, Εξάρτημα1.VCC, A1.pin4, J2.vcc, R1.Pin_0, R2.Pin_0

notes:
  R ≥ 220Ω
  Κόκκινο καλώδιο: 5V
  Λευκό καλώδιο: 3,3V

custom parts:
  Raspberry Pi Pico: Raspberry Pi Pico. Based around the RP2040 microcontroller the Pico is a low cost microcontroller device bringing Raspberry Pi quality, cost, and easy of use to the microcontroller space. Jan 2021, Split part in to two versions: tht (this one) and SMD. This one will drill holes for a .1 in header in pcb to allow plugging in the module as well as providing pads to solder the module to the top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
  LCD1602-I2C: A standard character display, usually with 2x16 characters. Comes in many colors with LCM1602 IIC attached.
  HuskyLens-Vision-Sensor_1: Huskylens is an easy-to-use AI Camera | Vision Sensor. DFrobot Huskylens is equipped with multiple functions, such as face recognition, object tracking, object recognition, line tracking, color recognition, and tag(QR code) recognition.
